# Fritzing sketch client_design (saved by Fritzing 0.9.3b)
breadboards: 1

parts:
  Part1 = Adafruit PN532 Breakout [part_number="Adafruit #364"]
  Raspberry_Pi_Zero1 = Raspberry Pi Zero
  LED1 = RGB LED (com. anode, rbg) [package="5 mm [THT]"]
  R1 = Resistor [tolerance=±5% resistance=220 package=THT]
  Q2 = MOSFET-NCHANNEL [package=to220v]
  R2 = Resistor [tolerance=±5% resistance=220 package=THT]
  R3 = Resistor [tolerance=±5% resistance=220 package=THT]
  Q3 = MOSFET-NCHANNEL [package=to220v]
  Q4 = MOSFET-NCHANNEL [package=to220v]

nets:
  N1: Part1.NSS/SCL/RX, Raspberry_Pi_Zero1.GPIO20
  GND: Part1.GND, Raspberry_Pi_Zero1.GND, LED1.common_anode
  3V3: Part1.VDD, Raspberry_Pi_Zero1.3v3, Raspberry_Pi_Zero1.3V3
  N2: Part1.SCK, Raspberry_Pi_Zero1.GPIO26
  N3: Part1.MISO, Raspberry_Pi_Zero1.GPIO19
  N4: Part1.MOSI/SDA/TX, Raspberry_Pi_Zero1.GPIO13
  N5: Raspberry_Pi_Zero1.GPIO17, Q3.G
  N6: Raspberry_Pi_Zero1.GPIO27, Q4.G
  N7: Raspberry_Pi_Zero1.GPIO14, Q2.G
  N8: Raspberry_Pi_Zero1.5V, Q2.S, Q3.S, Q4.S
  N9: LED1.red_cathode, R1.Pin_1
  N10: LED1.blue_cathode, R2.Pin_1
  N11: LED1.green_cathode, R3.Pin_1
  N12: R1.Pin_0, Q2.D
  N13: R2.Pin_0, Q3.D
  N14: R3.Pin_0, Q4.D

custom parts:
  Adafruit PN532 Breakout: The PN532 is the most popular NFC chip, and is what is embedded in pretty much every phone or device that does NFC. It can pretty much do it all, such as read and write to tags and cards, communicate with phones (say for payment processing), and 'act' like a NFC tag. If you want to do any sort of embedded NFC work, this is the chip you'll want to use! NFC (Near Field Communications) is a way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
